// Logisim project mips.circ as structural Verilog: 6 circuits, main circuit main
module main (
  input  Reset
);

  wire ALUSrc, and_1_out, Branch, Clock, Jump, MemRead, MemToReg, MemWrite, not_1_out, or_1_out, RegDst,
       RegWrite, Zero;
  wire [1:0] ALUOp;
  wire [2:0] ALU_Control_aluctrl, Funct, instruction_decoder_1_opcode, multiplexer_1_out, Rd, Rs, Rt, Shamt;
  wire [7:0] adder_1_out, Adress_IMM, alu_1_result, InstMemAddress, multiplexer_2_out, multiplexer_3_out,
       multiplexer_4_out, ram_1_data, Register_File_read_data_1, RtData;
  wire [17:0] rom_1_data;

  Clock clock_1 (.out(Clock));
  Multiplexer #(.width(3), .enable("false")) multiplexer_1 (.in0(Rt), .in1(Rd), .out(multiplexer_1_out), .sel(RegDst));
  Register_File Register_File (
    .Read_register_1(Rs), .Read_register_2(Rt), .Write_data(multiplexer_4_out),
    .Write_register(multiplexer_1_out), .RegWrite(RegWrite), .Clock(Clock), .Clear(Reset),
    .Read_data_1(Register_File_read_data_1), .Read_data_2(RtData));
  ALU_Control ALU_Control (.Funct(Funct), .ALUOp(ALUOp), .ALUCtrl(ALU_Control_aluctrl));
  Register PC (.D(multiplexer_3_out), .Q(InstMemAddress), .clk(Clock), .clr(Reset));  // open: en
  ROM #(.dataWidth(18)) rom_1 (.addr(InstMemAddress), .data(rom_1_data));  // open: sel
  Instruction_Decoder instruction_decoder_1 (
    .Instruction(rom_1_data), .Address_IMM(Adress_IMM), .Funct(Funct), .Shamt(Shamt), .Rd(Rd), .Rt(Rt),
    .Rs(Rs), .Opcode(instruction_decoder_1_opcode));
  Multiplexer #(.width(8), .enable("false")) multiplexer_2 (
    .in0(RtData), .in1(Adress_IMM), .out(multiplexer_2_out), .sel(ALUSrc));
  Adder adder_1 (.a(8'h1), .b(InstMemAddress), .out(adder_1_out));  // open: cin, cout
  and and_1 (and_1_out, Branch, Zero);
  ALU alu_1 (
    .A(Register_File_read_data_1), .B(multiplexer_2_out), .ALU_Control(ALU_Control_aluctrl),
    .Shift_Amount(Shamt), .Result(alu_1_result), .Zero_Flag(Zero));
  or or_1 (or_1_out, Jump, and_1_out);
  Multiplexer #(.width(8), .enable("false")) multiplexer_3 (
    .in0(adder_1_out), .in1(Adress_IMM), .out(multiplexer_3_out), .sel(or_1_out));
  Control_Unit control_unit_1 (
    .Opcode(instruction_decoder_1_opcode), .RegDst(RegDst), .RegWrite(RegWrite), .ALUSrc(ALUSrc),
    .MemWrite(MemWrite), .MemRead(MemRead), .MemToReg(MemToReg), .Branch(Branch), .Jump(Jump), .ALUOp(ALUOp));
  not not_1 (not_1_out, Clock);
  RAM #(.bus("separate")) ram_1 (
    .addr(alu_1_result), .din(RtData), .data(ram_1_data), .str(MemWrite), .clk(not_1_out), .ld(MemRead),
    .clr(Reset));  // open: sel
  Multiplexer #(.width(8), .enable("false")) multiplexer_4 (
    .in0(alu_1_result), .in1(ram_1_data), .out(multiplexer_4_out), .sel(MemToReg));
  ROM #(.dataWidth(18)) rom_2 ();  // open: addr, data, sel

  // Other names for the same wires on the sheet: Clear = Reset

  // Notes on the sheet:
  //   Clock
  //   Instruction Memory
  //   contents of rom_1 (hex, n*v repeats v):
  //   2020c 20408 14c0 20a06 20c07 5dc2 10e00
  //   Incrementer
  //   Opcode
  //   Data Memory
  //   Instruction Fetch Unit
  //   Instruction Decode Unit
  //   Execution Unit
  //   contents of rom_2 (hex, n*v repeats v):
  //   0 20403 14c0 0 20203 20404 14c2 0 0 2022a 10200 8400 22c0 0 2020a 10201 20414 10402 8201 8402 14c2
  //   10603
endmodule

module Register_File (
  input  [2:0] Read_register_1,
  input  [2:0] Read_register_2,
  input  [7:0] Write_data,
  input  [2:0] Write_register,
  input  RegWrite,
  input  Clock,
  input  Clear,
  output [7:0] Read_data_1,
  output [7:0] Read_data_2
);

  wire WE0, WE1, WE2, WE3, WE4, WE5, WE6, WE7;
  wire [7:0] Reg0, Reg1, Reg2, Reg3, Reg4, Reg5, Reg6, Reg7, Write0, Write1, Write2, Write3, Write4, Write5,
       Write6, Write7;

  Demultiplexer #(.select(3), .width(8), .enable("false")) demultiplexer_1 (
    .out0(Write0), .out1(Write1), .out2(Write2), .out3(Write3), .out4(Write4), .out5(Write5), .out6(Write6),
    .out7(Write7), .in(Write_data), .sel(Write_register));
  Demultiplexer #(.select(3), .enable("false")) demultiplexer_2 (
    .out0(WE0), .out1(WE1), .out2(WE2), .out3(WE3), .out4(WE4), .out5(WE5), .out6(WE6), .out7(WE7),
    .in(RegWrite), .sel(Write_register));
  Register u_Reg0 (.D(Write0), .en(WE0), .Q(Reg0), .clk(Clock), .clr(Clear));
  Register u_Reg1 (.D(Write1), .en(WE1), .Q(Reg1), .clk(Clock), .clr(Clear));
  Register u_Reg2 (.D(Write2), .en(WE2), .Q(Reg2), .clk(Clock), .clr(Clear));
  Register u_Reg3 (.D(Write3), .en(WE3), .Q(Reg3), .clk(Clock), .clr(Clear));
  Register u_Reg4 (.D(Write4), .en(WE4), .Q(Reg4), .clk(Clock), .clr(Clear));
  Register u_Reg5 (.D(Write5), .en(WE5), .Q(Reg5), .clk(Clock), .clr(Clear));
  Register u_Reg6 (.D(Write6), .en(WE6), .Q(Reg6), .clk(Clock), .clr(Clear));
  Register u_Reg7 (.D(Write7), .en(WE7), .Q(Reg7), .clk(Clock), .clr(Clear));
  Multiplexer #(.select(3), .width(8), .enable("false")) multiplexer_1 (
    .in0(Reg0), .in1(Reg1), .in2(Reg2), .in3(Reg3), .in4(Reg4), .in5(Reg5), .in6(Reg6), .in7(Reg7),
    .out(Read_data_1), .sel(Read_register_1));
  Multiplexer #(.select(3), .width(8), .enable("false")) multiplexer_2 (
    .in0(Reg0), .in1(Reg1), .in2(Reg2), .in3(Reg3), .in4(Reg4), .in5(Reg5), .in6(Reg6), .in7(Reg7),
    .out(Read_data_2), .sel(Read_register_2));

  // Other names for the same wires on the sheet: Read1[2:0] = Read_register_1; Read2[2:0] = Read_register_2
endmodule

module ALU (
  input  [7:0] A,
  input  [7:0] B,
  input  [2:0] ALU_Control,
  input  [2:0] Shift_Amount,
  output [7:0] Result,
  output Zero_Flag
);

  wire comparator_1_lt, Z;
  wire [7:0] AAdd, ADiv, AMul, ANeg, ASLL, ASLT, ASRL, ASub, BAdd, BDiv, BMul, BSLT, BSub, RAdd, RDiv, RMul,
       RNeg, RSLL, RSLT, RSRL, RSub;

  Demultiplexer #(.select(3), .width(8), .enable("false")) demultiplexer_1 (
    .out0(AAdd), .out1(ASub), .out2(AMul), .out3(ADiv), .out4(ANeg), .out5(ASLT), .out6(ASLL), .out7(ASRL),
    .in(A), .sel(ALU_Control));
  Demultiplexer #(.select(3), .width(8), .enable("false")) demultiplexer_2 (
    .out0(BAdd), .out1(BSub), .out2(BMul), .out3(BDiv), .out5(BSLT), .in(B), .sel(ALU_Control));  // open: out4, out6, out7
  Adder adder_1 (.a(AAdd), .b(BAdd), .out(RAdd));  // open: cin, cout
  Subtractor subtractor_1 (.a(ASub), .b(BSub), .out(RSub));  // open: bin, bout
  Multiplier multiplier_1 (.a(AMul), .b(BMul), .out(RMul));  // open: cin, cout
  Divider divider_1 (.a(ADiv), .b(BDiv), .out(RDiv));  // open: upper, rem
  Negator negator_1 (.in(ANeg), .out(RNeg));
  Comparator comparator_1 (.a(ASLT), .b(BSLT), .eq(Z), .lt(comparator_1_lt));  // open: gt
  Shifter shifter_1 (.in(ASLL), .\dist (Shift_Amount), .out(RSLL));
  Shifter #(.shift("lr")) shifter_2 (.in(ASRL), .\dist (Shift_Amount), .out(RSRL));
  assign RSLT = {{7{1'b0}}, comparator_1_lt};  // Bit_Extender bit_extender_1
  Multiplexer #(.select(3), .width(8), .enable("false")) multiplexer_1 (
    .in0(RAdd), .in1(RSub), .in2(RMul), .in3(RDiv), .in4(RNeg), .in5(RSLT), .in6(RSLL), .in7(RSRL),
    .out(Result), .sel(ALU_Control));
  Comparator comparator_2 (.a(A), .b(B), .eq(Zero_Flag));  // open: gt, lt

  // Other names for the same wires on the sheet: ALUCtrl[2:0] = ALU_Control; Shamt[2:0] = Shift_Amount
endmodule

module Control_Unit (
  input  [2:0] Opcode,
  output RegDst,
  output RegWrite,
  output ALUSrc,
  output MemWrite,
  output MemRead,
  output MemToReg,
  output Branch,
  output Jump,
  output [1:0] ALUOp
);

  wire _100, _101, _110;

  Demultiplexer #(.select(3), .enable("false")) demultiplexer_1 (
    .out0(RegDst), .out1(MemRead), .out2(MemWrite), .out3(Branch), .out4(_100), .out5(_101), .out6(_110),
    .out7(Jump), .in(1'b1), .sel(Opcode));
  or or_1 (RegWrite, RegDst, MemRead, _100);
  or or_2 (ALUSrc, MemRead, MemWrite, _100, Jump);
  or or_3 (ALUOp[0], Branch, _100);
  or or_4 (ALUOp[1], RegDst, _100);

  assign MemToReg = MemRead;

  // Other names for the same wires on the sheet: _000 = RegDst; _001 = MemRead; _010 = MemWrite; _011 = Branch;
  //   _111 = Jump
endmodule

module ALU_Control (
  input  [2:0] Funct,
  input  [1:0] ALUOp,
  output [2:0] ALUCtrl
);

  Multiplexer #(.select(2), .width(3), .enable("false")) multiplexer_1 (
    .in0(3'b000), .in1(3'b101), .in2(Funct), .in3(3'b000), .out(ALUCtrl), .sel(ALUOp));
endmodule

module Instruction_Decoder (
  input  [17:0] Instruction,
  output [7:0] Address_IMM,
  output [2:0] Funct,
  output [2:0] Shamt,
  output [2:0] Rd,
  output [2:0] Rt,
  output [2:0] Rs,
  output [2:0] Opcode
);


  assign Address_IMM = Instruction[7:0];
  assign Funct = Instruction[2:0];
  assign Opcode = Instruction[17:15];
  assign Rd = Instruction[8:6];
  assign Rs = Instruction[14:12];
  assign Rt = Instruction[11:9];
  assign Shamt = Instruction[5:3];
endmodule
